// Logisim project MyAdder.circ as structural Verilog: 7 circuits, main circuit main
module main (
  input  in_1,
  input  in_2,
  input  in_3,
  input  in_4,
  input  in_5,
  input  in_6,
  input  in_7,
  input  in_8
);

  wire fulladder_4_1_s0, fulladder_4_1_s1, fulladder_4_1_s2, fulladder_4_1_s3,
       segmentdisplaydecoder_7_16_1_a, segmentdisplaydecoder_7_16_1_b, segmentdisplaydecoder_7_16_1_c,
       segmentdisplaydecoder_7_16_1_d, segmentdisplaydecoder_7_16_1_e, segmentdisplaydecoder_7_16_1_f,
       segmentdisplaydecoder_7_16_1_g, segmentdisplaydecoder_7_16_2_a, segmentdisplaydecoder_7_16_2_b,
       segmentdisplaydecoder_7_16_2_c, segmentdisplaydecoder_7_16_2_d, segmentdisplaydecoder_7_16_2_e,
       segmentdisplaydecoder_7_16_2_f, segmentdisplaydecoder_7_16_2_g, segmentdisplaydecoder_7_16_3_a,
       segmentdisplaydecoder_7_16_3_b, segmentdisplaydecoder_7_16_3_c, segmentdisplaydecoder_7_16_3_d,
       segmentdisplaydecoder_7_16_3_e, segmentdisplaydecoder_7_16_3_f, segmentdisplaydecoder_7_16_3_g;

  FullAdder_4 fulladder_4_1 (
    .A0(in_1), .B0(in_5), .A1(in_2), .B1(in_6), .A2(in_3), .B2(in_7), .A3(in_4), .B3(in_8),
    .S0(fulladder_4_1_s0), .S1(fulladder_4_1_s1), .S2(fulladder_4_1_s2), .S3(fulladder_4_1_s3));  // open: C4
  SegmentDisplayDecoder_7_16 segmentdisplaydecoder_7_16_1 (
    .in_1(in_1), .in_2(in_2), .in_3(in_3), .in_4(in_4), .A(segmentdisplaydecoder_7_16_1_a),
    .B(segmentdisplaydecoder_7_16_1_b), .C(segmentdisplaydecoder_7_16_1_c),
    .D(segmentdisplaydecoder_7_16_1_d), .E(segmentdisplaydecoder_7_16_1_e),
    .F(segmentdisplaydecoder_7_16_1_f), .G(segmentdisplaydecoder_7_16_1_g));
  SegmentDisplayDecoder_7_16 segmentdisplaydecoder_7_16_2 (
    .in_1(in_5), .in_2(in_6), .in_3(in_7), .in_4(in_8), .A(segmentdisplaydecoder_7_16_2_a),
    .B(segmentdisplaydecoder_7_16_2_b), .C(segmentdisplaydecoder_7_16_2_c),
    .D(segmentdisplaydecoder_7_16_2_d), .E(segmentdisplaydecoder_7_16_2_e),
    .F(segmentdisplaydecoder_7_16_2_f), .G(segmentdisplaydecoder_7_16_2_g));
  _7_Segment_Display u_7_segment_display_1 (
    .g(segmentdisplaydecoder_7_16_1_g), .f(segmentdisplaydecoder_7_16_1_f),
    .a(segmentdisplaydecoder_7_16_1_a), .b(segmentdisplaydecoder_7_16_1_b),
    .e(segmentdisplaydecoder_7_16_1_e), .d(segmentdisplaydecoder_7_16_1_d), .c(segmentdisplaydecoder_7_16_1_c));  // open: dp
  _7_Segment_Display u_7_segment_display_2 (
    .g(segmentdisplaydecoder_7_16_2_g), .f(segmentdisplaydecoder_7_16_2_f),
    .a(segmentdisplaydecoder_7_16_2_a), .b(segmentdisplaydecoder_7_16_2_b),
    .e(segmentdisplaydecoder_7_16_2_e), .d(segmentdisplaydecoder_7_16_2_d), .c(segmentdisplaydecoder_7_16_2_c));  // open: dp
  SegmentDisplayDecoder_7_16 segmentdisplaydecoder_7_16_3 (
    .in_1(fulladder_4_1_s0), .in_2(fulladder_4_1_s1), .in_3(fulladder_4_1_s2), .in_4(fulladder_4_1_s3),
    .A(segmentdisplaydecoder_7_16_3_a), .B(segmentdisplaydecoder_7_16_3_b),
    .C(segmentdisplaydecoder_7_16_3_c), .D(segmentdisplaydecoder_7_16_3_d),
    .E(segmentdisplaydecoder_7_16_3_e), .F(segmentdisplaydecoder_7_16_3_f), .G(segmentdisplaydecoder_7_16_3_g));
  _7_Segment_Display u_7_segment_display_3 (
    .g(segmentdisplaydecoder_7_16_3_g), .f(segmentdisplaydecoder_7_16_3_f),
    .a(segmentdisplaydecoder_7_16_3_a), .b(segmentdisplaydecoder_7_16_3_b),
    .e(segmentdisplaydecoder_7_16_3_e), .d(segmentdisplaydecoder_7_16_3_d), .c(segmentdisplaydecoder_7_16_3_c));  // open: dp
endmodule

module FullAdder (
  input  in_1,
  input  in_2,
  input  in_3,
  output out_4,
  output out_5
);

  wire and_1_out, and_2_out, xor_1_out;

  xor xor_1 (xor_1_out, in_1, in_2);
  and and_1 (and_1_out, in_1, in_2);
  and and_2 (and_2_out, xor_1_out, in_3);
  xor xor_2 (out_4, xor_1_out, in_3);
  or or_1 (out_5, and_1_out, and_2_out);
endmodule

module Decoder_2to4 (
  input  EN,
  input  in_2,
  input  in_3,
  output out_4,
  output out_5,
  output out_6,
  output out_7
);

  wire not_1_out, not_2_out;

  not not_1 (not_1_out, in_2);
  not not_2 (not_2_out, in_3);
  and and_1 (out_4, not_1_out, EN, not_2_out);
  and and_2 (out_5, in_2, EN, not_2_out);
  and and_3 (out_6, not_1_out, EN, in_3);
  and and_4 (out_7, in_2, EN, in_3);

  // Notes on the sheet:
  //   2- 4译码器
endmodule

module Decoder_3to8 (
  input  in_1,
  input  in_2,
  input  in_3,
  input  EN,
  output out_5,
  output out_6,
  output out_7,
  output out_8,
  output out_9,
  output out_10,
  output out_11,
  output out_12
);

  wire and_1_out, and_2_out, not_1_out;

  not not_1 (not_1_out, in_3);
  and and_1 (and_1_out, EN, not_1_out);
  and and_2 (and_2_out, in_3, EN);
  Decoder_2to4 decoder_2to4_1 (
    .EN(and_1_out), .in_2(in_1), .in_3(in_2), .out_4(out_5), .out_5(out_6), .out_6(out_7), .out_7(out_8));
  Decoder_2to4 decoder_2to4_2 (
    .EN(and_2_out), .in_2(in_1), .in_3(in_2), .out_4(out_9), .out_5(out_10), .out_6(out_11), .out_7(out_12));
endmodule

module SegmentDisplayDecoder_7_10 (
  input  in_1,
  input  in_2,
  input  in_3,
  input  in_4
);

  wire a_out, b_out, c_out, d_out, decoder_3to8_1_out_5, decoder_3to8_1_out_6, decoder_3to8_1_out_7,
       decoder_3to8_1_out_8, decoder_3to8_1_out_9, decoder_3to8_1_out_10, decoder_3to8_1_out_11,
       decoder_3to8_1_out_12, decoder_3to8_2_out_5, decoder_3to8_2_out_6, decoder_3to8_2_out_7,
       decoder_3to8_2_out_8, decoder_3to8_2_out_9, decoder_3to8_2_out_10, decoder_3to8_2_out_11,
       decoder_3to8_2_out_12, e_out, f_out, g_out, not_1_out, or_1_out;

  not not_1 (not_1_out, in_4);
  or or_1 (or_1_out, decoder_3to8_2_out_9, decoder_3to8_2_out_7, decoder_3to8_2_out_8, decoder_3to8_2_out_10, decoder_3to8_2_out_11, decoder_3to8_2_out_12);
  Decoder_3to8 decoder_3to8_1 (
    .in_1(in_1), .in_2(in_2), .in_3(in_3), .EN(not_1_out), .out_5(decoder_3to8_1_out_5),
    .out_6(decoder_3to8_1_out_6), .out_7(decoder_3to8_1_out_7), .out_8(decoder_3to8_1_out_8),
    .out_9(decoder_3to8_1_out_9), .out_10(decoder_3to8_1_out_10), .out_11(decoder_3to8_1_out_11),
    .out_12(decoder_3to8_1_out_12));
  Decoder_3to8 decoder_3to8_2 (
    .in_1(in_1), .in_2(in_2), .in_3(in_3), .EN(in_4), .out_5(decoder_3to8_2_out_5),
    .out_6(decoder_3to8_2_out_6), .out_7(decoder_3to8_2_out_7), .out_8(decoder_3to8_2_out_8),
    .out_9(decoder_3to8_2_out_9), .out_10(decoder_3to8_2_out_10), .out_11(decoder_3to8_2_out_11),
    .out_12(decoder_3to8_2_out_12));
  or a (a_out, decoder_3to8_1_out_11, decoder_3to8_1_out_5, decoder_3to8_1_out_7, decoder_3to8_1_out_8, decoder_3to8_1_out_10, decoder_3to8_1_out_12, decoder_3to8_2_out_5, decoder_3to8_2_out_6);
  or b (b_out, decoder_3to8_1_out_5, decoder_3to8_1_out_6, decoder_3to8_1_out_7, decoder_3to8_1_out_8, decoder_3to8_1_out_9, decoder_3to8_1_out_12, decoder_3to8_2_out_5, decoder_3to8_2_out_6);
  or c (c_out, decoder_3to8_1_out_5, decoder_3to8_1_out_6, decoder_3to8_1_out_8, decoder_3to8_1_out_9, decoder_3to8_1_out_10, decoder_3to8_1_out_11, decoder_3to8_1_out_12, decoder_3to8_2_out_5, decoder_3to8_2_out_6);
  or d (d_out, decoder_3to8_1_out_5, decoder_3to8_1_out_7, decoder_3to8_1_out_8, decoder_3to8_1_out_10, decoder_3to8_1_out_11, decoder_3to8_2_out_5);
  or e (e_out, decoder_3to8_1_out_5, decoder_3to8_1_out_7, decoder_3to8_1_out_11, decoder_3to8_2_out_5);
  or f (f_out, decoder_3to8_1_out_5, decoder_3to8_1_out_9, decoder_3to8_1_out_10, decoder_3to8_1_out_11, decoder_3to8_2_out_5, decoder_3to8_2_out_6);
  or g (g_out, decoder_3to8_1_out_7, decoder_3to8_1_out_8, decoder_3to8_1_out_9, decoder_3to8_1_out_10, decoder_3to8_1_out_11, decoder_3to8_2_out_5, decoder_3to8_2_out_6);
  _7_Segment_Display u_7_segment_display_1 (
    .g(g_out), .f(f_out), .a(a_out), .b(b_out), .e(e_out), .d(d_out), .c(c_out), .dp(or_1_out));
endmodule

module SegmentDisplayDecoder_7_16 (
  input  in_1,
  input  in_2,
  input  in_3,
  input  in_4,
  output A,
  output B,
  output C,
  output D,
  output E,
  output F,
  output G
);

  wire decoder_3to8_1_out_5, decoder_3to8_1_out_6, decoder_3to8_1_out_7, decoder_3to8_1_out_8,
       decoder_3to8_1_out_9, decoder_3to8_1_out_10, decoder_3to8_1_out_11, decoder_3to8_1_out_12,
       decoder_3to8_2_out_5, decoder_3to8_2_out_6, decoder_3to8_2_out_7, decoder_3to8_2_out_8,
       decoder_3to8_2_out_9, decoder_3to8_2_out_10, decoder_3to8_2_out_11, decoder_3to8_2_out_12, not_1_out,
       or_1_out, or_2_out, or_3_out, or_4_out, or_5_out, or_6_out, or_7_out;

  not not_1 (not_1_out, in_4);
  Decoder_3to8 decoder_3to8_1 (
    .in_1(in_1), .in_2(in_2), .in_3(in_3), .EN(not_1_out), .out_5(decoder_3to8_1_out_5),
    .out_6(decoder_3to8_1_out_6), .out_7(decoder_3to8_1_out_7), .out_8(decoder_3to8_1_out_8),
    .out_9(decoder_3to8_1_out_9), .out_10(decoder_3to8_1_out_10), .out_11(decoder_3to8_1_out_11),
    .out_12(decoder_3to8_1_out_12));
  // NoConnect on decoder_3to8_2_out_5
  Decoder_3to8 decoder_3to8_2 (
    .in_1(in_1), .in_2(in_2), .in_3(in_3), .EN(in_4), .out_5(decoder_3to8_2_out_5),
    .out_6(decoder_3to8_2_out_6), .out_7(decoder_3to8_2_out_7), .out_8(decoder_3to8_2_out_8),
    .out_9(decoder_3to8_2_out_9), .out_10(decoder_3to8_2_out_10), .out_11(decoder_3to8_2_out_11),
    .out_12(decoder_3to8_2_out_12));
  or or_1 (or_1_out, decoder_3to8_1_out_6, decoder_3to8_1_out_9, decoder_3to8_2_out_8, decoder_3to8_2_out_10);
  not not_2 (A, or_1_out);
  or or_2 (or_2_out, decoder_3to8_1_out_10, decoder_3to8_1_out_11, decoder_3to8_2_out_8, decoder_3to8_2_out_9, decoder_3to8_2_out_11, decoder_3to8_2_out_12);
  not not_3 (B, or_2_out);
  or or_3 (or_3_out, decoder_3to8_1_out_7, decoder_3to8_2_out_9, decoder_3to8_2_out_11, decoder_3to8_2_out_12);
  not not_4 (C, or_3_out);
  or or_4 (or_4_out, decoder_3to8_1_out_6, decoder_3to8_1_out_9, decoder_3to8_1_out_12, decoder_3to8_2_out_7, decoder_3to8_2_out_12);
  not not_5 (D, or_4_out);
  or or_5 (or_5_out, decoder_3to8_1_out_6, decoder_3to8_1_out_8, decoder_3to8_1_out_9, decoder_3to8_1_out_10, decoder_3to8_1_out_12, decoder_3to8_2_out_6);
  not not_6 (E, or_5_out);
  or or_6 (or_6_out, decoder_3to8_1_out_6, decoder_3to8_1_out_7, decoder_3to8_1_out_8, decoder_3to8_1_out_12, decoder_3to8_2_out_10);
  not not_7 (F, or_6_out);
  or or_7 (or_7_out, decoder_3to8_1_out_5, decoder_3to8_1_out_6, decoder_3to8_1_out_12, decoder_3to8_2_out_9);
  not not_8 (G, or_7_out);
  _7_Segment_Display u_7_segment_display_1 (.g(G), .f(F), .a(A), .b(B), .e(E), .d(D), .c(C));  // open: dp
endmodule

module FullAdder_4 (
  input  A0,
  input  B0,
  input  A1,
  input  B1,
  input  A2,
  input  B2,
  input  A3,
  input  B3,
  output S0,
  output S1,
  output S2,
  output S3,
  output C4
);

  wire fulladder_1_out_5, fulladder_2_out_5, fulladder_3_out_5;

  FullAdder fulladder_1 (.in_1(A0), .in_2(B0), .in_3(1'b0), .out_4(S0), .out_5(fulladder_1_out_5));
  FullAdder fulladder_2 (.in_1(A1), .in_2(B1), .in_3(fulladder_1_out_5), .out_4(S1), .out_5(fulladder_2_out_5));
  FullAdder fulladder_3 (.in_1(A2), .in_2(B2), .in_3(fulladder_2_out_5), .out_4(S2), .out_5(fulladder_3_out_5));
  FullAdder fulladder_4 (.in_1(A3), .in_2(B3), .in_3(fulladder_3_out_5), .out_4(S3), .out_5(C4));
endmodule
