// Logisim project PriorityEncoder_16to4.circ as structural Verilog: 7 circuits, main circuit main
module main (
  input  Num0,
  input  Num1,
  input  Num2,
  input  Num3,
  input  Num4,
  input  Num5,
  input  Num6,
  input  Num7,
  input  Num8,
  input  Num9,
  input  in_11,
  input  in_12,
  input  in_13,
  input  in_14,
  input  in_15,
  input  in_16
);

  wire a_out, b_out, c_out, d_out, decoder_3to8_1_out_5, decoder_3to8_1_out_6, decoder_3to8_1_out_7,
       decoder_3to8_1_out_8, decoder_3to8_1_out_9, decoder_3to8_1_out_10, decoder_3to8_1_out_11,
       decoder_3to8_1_out_12, decoder_3to8_2_out_5, decoder_3to8_2_out_6, decoder_3to8_2_out_7,
       decoder_3to8_2_out_8, decoder_3to8_2_out_9, decoder_3to8_2_out_10, decoder_3to8_2_out_11,
       decoder_3to8_2_out_12, e_out, f_out, g_out, not_1_out, or_1_out, priorityencoder_16to4_1_out_17,
       priorityencoder_16to4_1_out_18, priorityencoder_16to4_1_out_19, priorityencoder_16to4_1_out_20;

  PriorityEncoder_16to4 priorityencoder_16to4_1 (
    .in_1(Num0), .in_2(Num1), .in_3(Num2), .in_4(Num3), .in_5(Num4), .in_6(Num5), .in_7(Num6), .in_8(Num7),
    .in_9(Num8), .in_10(Num9), .in_11(in_11), .in_12(in_12), .in_13(in_13), .in_14(in_14), .in_15(in_15),
    .in_16(in_16), .out_17(priorityencoder_16to4_1_out_17), .out_18(priorityencoder_16to4_1_out_18),
    .out_19(priorityencoder_16to4_1_out_19), .out_20(priorityencoder_16to4_1_out_20));
  not not_1 (not_1_out, priorityencoder_16to4_1_out_20);
  or or_1 (or_1_out, decoder_3to8_2_out_9, decoder_3to8_2_out_7, decoder_3to8_2_out_8, decoder_3to8_2_out_10, decoder_3to8_2_out_11, decoder_3to8_2_out_12);
  Decoder_3to8 decoder_3to8_1 (
    .in_1(priorityencoder_16to4_1_out_17), .in_2(priorityencoder_16to4_1_out_18),
    .in_3(priorityencoder_16to4_1_out_19), .EN(not_1_out), .out_5(decoder_3to8_1_out_5),
    .out_6(decoder_3to8_1_out_6), .out_7(decoder_3to8_1_out_7), .out_8(decoder_3to8_1_out_8),
    .out_9(decoder_3to8_1_out_9), .out_10(decoder_3to8_1_out_10), .out_11(decoder_3to8_1_out_11),
    .out_12(decoder_3to8_1_out_12));
  Decoder_3to8 decoder_3to8_2 (
    .in_1(priorityencoder_16to4_1_out_17), .in_2(priorityencoder_16to4_1_out_18),
    .in_3(priorityencoder_16to4_1_out_19), .EN(priorityencoder_16to4_1_out_20), .out_5(decoder_3to8_2_out_5),
    .out_6(decoder_3to8_2_out_6), .out_7(decoder_3to8_2_out_7), .out_8(decoder_3to8_2_out_8),
    .out_9(decoder_3to8_2_out_9), .out_10(decoder_3to8_2_out_10), .out_11(decoder_3to8_2_out_11),
    .out_12(decoder_3to8_2_out_12));
  or a (a_out, decoder_3to8_1_out_11, decoder_3to8_1_out_5, decoder_3to8_1_out_7, decoder_3to8_1_out_8, decoder_3to8_1_out_10, decoder_3to8_1_out_12, decoder_3to8_2_out_5, decoder_3to8_2_out_6);
  or b (b_out, decoder_3to8_1_out_5, decoder_3to8_1_out_6, decoder_3to8_1_out_7, decoder_3to8_1_out_8, decoder_3to8_1_out_9, decoder_3to8_1_out_12, decoder_3to8_2_out_5, decoder_3to8_2_out_6);
  or c (c_out, decoder_3to8_1_out_5, decoder_3to8_1_out_6, decoder_3to8_1_out_8, decoder_3to8_1_out_9, decoder_3to8_1_out_10, decoder_3to8_1_out_11, decoder_3to8_1_out_12, decoder_3to8_2_out_5, decoder_3to8_2_out_6);
  or d (d_out, decoder_3to8_1_out_5, decoder_3to8_1_out_7, decoder_3to8_1_out_8, decoder_3to8_1_out_10, decoder_3to8_1_out_11, decoder_3to8_2_out_5);
  or e (e_out, decoder_3to8_1_out_5, decoder_3to8_1_out_7, decoder_3to8_1_out_11, decoder_3to8_2_out_5);
  or f (f_out, decoder_3to8_1_out_5, decoder_3to8_1_out_9, decoder_3to8_1_out_10, decoder_3to8_1_out_11, decoder_3to8_2_out_5, decoder_3to8_2_out_6);
  or g (g_out, decoder_3to8_1_out_7, decoder_3to8_1_out_8, decoder_3to8_1_out_9, decoder_3to8_1_out_10, decoder_3to8_1_out_11, decoder_3to8_2_out_5, decoder_3to8_2_out_6);
  _7_Segment_Display u_7_segment_display_1 (
    .g(g_out), .f(f_out), .a(a_out), .b(b_out), .e(e_out), .d(d_out), .c(c_out), .dp(or_1_out));
endmodule

module PriorityEncoder_4to2 (
  input  in_1,
  input  in_2,
  input  in_3,
  input  in_4,
  output out_5,
  output out_6
);

  wire and_1_out, and_2_out, not_1_out, not_2_out;

  // NoConnect on in_1
  and and_1 (and_1_out, in_2, not_1_out);
  not not_1 (not_1_out, in_3);
  and and_2 (and_2_out, in_3, not_2_out);
  not not_2 (not_2_out, in_4);
  or or_1 (out_5, in_4, and_1_out);
  or or_2 (out_6, and_2_out, in_4);
endmodule

module PriorityEncoder_16to4 (
  input  in_1,
  input  in_2,
  input  in_3,
  input  in_4,
  input  in_5,
  input  in_6,
  input  in_7,
  input  in_8,
  input  in_9,
  input  in_10,
  input  in_11,
  input  in_12,
  input  in_13,
  input  in_14,
  input  in_15,
  input  in_16,
  output out_17,
  output out_18,
  output out_19,
  output out_20
);

  wire or_1_out, or_2_out, or_3_out, or_4_out, priorityencoder_4to2_1_out_5, priorityencoder_4to2_1_out_6,
       priorityencoder_4to2_2_out_5, priorityencoder_4to2_2_out_6, priorityencoder_4to2_3_out_5,
       priorityencoder_4to2_3_out_6, priorityencoder_4to2_4_out_5, priorityencoder_4to2_4_out_6;

  or or_1 (or_1_out, in_1, in_2, in_3, in_4);
  or or_2 (or_2_out, in_5, in_6, in_7, in_8);
  or or_3 (or_3_out, in_9, in_10, in_11, in_12);
  or or_4 (or_4_out, in_13, in_14, in_15, in_16);
  PriorityEncoder_4to2 priorityencoder_4to2_1 (
    .in_1(in_1), .in_2(in_2), .in_3(in_3), .in_4(in_4), .out_5(priorityencoder_4to2_1_out_5),
    .out_6(priorityencoder_4to2_1_out_6));
  PriorityEncoder_4to2 priorityencoder_4to2_2 (
    .in_1(in_5), .in_2(in_6), .in_3(in_7), .in_4(in_8), .out_5(priorityencoder_4to2_2_out_5),
    .out_6(priorityencoder_4to2_2_out_6));
  PriorityEncoder_4to2 priorityencoder_4to2_3 (
    .in_1(in_9), .in_2(in_10), .in_3(in_11), .in_4(in_12), .out_5(priorityencoder_4to2_3_out_5),
    .out_6(priorityencoder_4to2_3_out_6));
  PriorityEncoder_4to2 priorityencoder_4to2_4 (
    .in_1(in_13), .in_2(in_14), .in_3(in_15), .in_4(in_16), .out_5(priorityencoder_4to2_4_out_5),
    .out_6(priorityencoder_4to2_4_out_6));
  PriorityEncoder_4to2 priorityencoder_4to2_5 (
    .in_1(or_1_out), .in_2(or_2_out), .in_3(or_3_out), .in_4(or_4_out), .out_5(out_19), .out_6(out_20));
  Mux_4to1 mux_4to1_1 (
    .in_1(priorityencoder_4to2_1_out_5), .in_2(priorityencoder_4to2_2_out_5),
    .in_3(priorityencoder_4to2_3_out_5), .in_4(priorityencoder_4to2_4_out_5), .in_5(out_19), .in_6(out_20),
    .out_7(out_17));
  Mux_4to1 mux_4to1_2 (
    .in_1(priorityencoder_4to2_1_out_6), .in_2(priorityencoder_4to2_2_out_6),
    .in_3(priorityencoder_4to2_3_out_6), .in_4(priorityencoder_4to2_4_out_6), .in_5(out_19), .in_6(out_20),
    .out_7(out_18));
endmodule

module Decoder_2to4 (
  input  EN,
  input  in_2,
  input  in_3,
  output out_4,
  output out_5,
  output out_6,
  output out_7
);

  wire not_1_out, not_2_out;

  not not_1 (not_1_out, in_2);
  not not_2 (not_2_out, in_3);
  and and_1 (out_4, not_1_out, EN, not_2_out);
  and and_2 (out_5, in_2, EN, not_2_out);
  and and_3 (out_6, not_1_out, EN, in_3);
  and and_4 (out_7, in_2, EN, in_3);

  // Notes on the sheet:
  //   2- 4译码器
endmodule

module Decoder_3to8 (
  input  in_1,
  input  in_2,
  input  in_3,
  input  EN,
  output out_5,
  output out_6,
  output out_7,
  output out_8,
  output out_9,
  output out_10,
  output out_11,
  output out_12
);

  wire and_1_out, and_2_out, not_1_out;

  not not_1 (not_1_out, in_3);
  and and_1 (and_1_out, EN, not_1_out);
  and and_2 (and_2_out, in_3, EN);
  Decoder_2to4 decoder_2to4_1 (
    .EN(and_1_out), .in_2(in_1), .in_3(in_2), .out_4(out_5), .out_5(out_6), .out_6(out_7), .out_7(out_8));
  Decoder_2to4 decoder_2to4_2 (
    .EN(and_2_out), .in_2(in_1), .in_3(in_2), .out_4(out_9), .out_5(out_10), .out_6(out_11), .out_7(out_12));
endmodule

module SegmentDisplayDecoder_7 (
  input  in_1,
  input  in_2,
  input  in_3,
  input  in_4
);

  wire a_out, b_out, c_out, d_out, decoder_3to8_1_out_5, decoder_3to8_1_out_6, decoder_3to8_1_out_7,
       decoder_3to8_1_out_8, decoder_3to8_1_out_9, decoder_3to8_1_out_10, decoder_3to8_1_out_11,
       decoder_3to8_1_out_12, decoder_3to8_2_out_5, decoder_3to8_2_out_6, decoder_3to8_2_out_7,
       decoder_3to8_2_out_8, decoder_3to8_2_out_9, decoder_3to8_2_out_10, decoder_3to8_2_out_11,
       decoder_3to8_2_out_12, e_out, f_out, g_out, not_1_out, or_1_out;

  not not_1 (not_1_out, in_4);
  or or_1 (or_1_out, decoder_3to8_2_out_9, decoder_3to8_2_out_7, decoder_3to8_2_out_8, decoder_3to8_2_out_10, decoder_3to8_2_out_11, decoder_3to8_2_out_12);
  Decoder_3to8 decoder_3to8_1 (
    .in_1(in_1), .in_2(in_2), .in_3(in_3), .EN(not_1_out), .out_5(decoder_3to8_1_out_5),
    .out_6(decoder_3to8_1_out_6), .out_7(decoder_3to8_1_out_7), .out_8(decoder_3to8_1_out_8),
    .out_9(decoder_3to8_1_out_9), .out_10(decoder_3to8_1_out_10), .out_11(decoder_3to8_1_out_11),
    .out_12(decoder_3to8_1_out_12));
  Decoder_3to8 decoder_3to8_2 (
    .in_1(in_1), .in_2(in_2), .in_3(in_3), .EN(in_4), .out_5(decoder_3to8_2_out_5),
    .out_6(decoder_3to8_2_out_6), .out_7(decoder_3to8_2_out_7), .out_8(decoder_3to8_2_out_8),
    .out_9(decoder_3to8_2_out_9), .out_10(decoder_3to8_2_out_10), .out_11(decoder_3to8_2_out_11),
    .out_12(decoder_3to8_2_out_12));
  or a (a_out, decoder_3to8_1_out_11, decoder_3to8_1_out_5, decoder_3to8_1_out_7, decoder_3to8_1_out_8, decoder_3to8_1_out_10, decoder_3to8_1_out_12, decoder_3to8_2_out_5, decoder_3to8_2_out_6);
  or b (b_out, decoder_3to8_1_out_5, decoder_3to8_1_out_6, decoder_3to8_1_out_7, decoder_3to8_1_out_8, decoder_3to8_1_out_9, decoder_3to8_1_out_12, decoder_3to8_2_out_5, decoder_3to8_2_out_6);
  or c (c_out, decoder_3to8_1_out_5, decoder_3to8_1_out_6, decoder_3to8_1_out_8, decoder_3to8_1_out_9, decoder_3to8_1_out_10, decoder_3to8_1_out_11, decoder_3to8_1_out_12, decoder_3to8_2_out_5, decoder_3to8_2_out_6);
  or d (d_out, decoder_3to8_1_out_5, decoder_3to8_1_out_7, decoder_3to8_1_out_8, decoder_3to8_1_out_10, decoder_3to8_1_out_11, decoder_3to8_2_out_5);
  or e (e_out, decoder_3to8_1_out_5, decoder_3to8_1_out_7, decoder_3to8_1_out_11, decoder_3to8_2_out_5);
  or f (f_out, decoder_3to8_1_out_5, decoder_3to8_1_out_9, decoder_3to8_1_out_10, decoder_3to8_1_out_11, decoder_3to8_2_out_5, decoder_3to8_2_out_6);
  or g (g_out, decoder_3to8_1_out_7, decoder_3to8_1_out_8, decoder_3to8_1_out_9, decoder_3to8_1_out_10, decoder_3to8_1_out_11, decoder_3to8_2_out_5, decoder_3to8_2_out_6);
  _7_Segment_Display u_7_segment_display_1 (
    .g(g_out), .f(f_out), .a(a_out), .b(b_out), .e(e_out), .d(d_out), .c(c_out), .dp(or_1_out));
endmodule

module Mux_4to1 (
  input  in_1,
  input  in_2,
  input  in_3,
  input  in_4,
  input  in_5,
  input  in_6,
  output out_7
);

  wire and_1_out, and_2_out, and_3_out, and_4_out;

  and and_1 (and_1_out, in_1, ~in_5, ~in_6);  // AND_Gate
  and and_2 (and_2_out, in_2, in_5, ~in_6);  // AND_Gate
  and and_3 (and_3_out, in_3, ~in_5, in_6);  // AND_Gate
  and and_4 (and_4_out, in_4, in_5, in_6);
  or or_1 (out_7, and_1_out, and_2_out, and_3_out, and_4_out);
endmodule
