// Logisim project 7_SegmentDisplayDecoder.circ as structural Verilog: 4 circuits, main circuit main
module main (
  input  in_1,
  input  in_2,
  input  in_3,
  input  in_4
);

  wire a_out, b_out, c_out, d_out, decoder_3to8_1_out_5, decoder_3to8_1_out_6, decoder_3to8_1_out_7,
       decoder_3to8_1_out_8, decoder_3to8_1_out_9, decoder_3to8_1_out_10, decoder_3to8_1_out_11,
       decoder_3to8_1_out_12, decoder_3to8_2_out_5, decoder_3to8_2_out_6, decoder_3to8_2_out_7,
       decoder_3to8_2_out_8, decoder_3to8_2_out_9, decoder_3to8_2_out_10, decoder_3to8_2_out_11,
       decoder_3to8_2_out_12, e_out, f_out, g_out, not_1_out, or_1_out;

  not not_1 (not_1_out, in_4);
  or or_1 (or_1_out, decoder_3to8_2_out_9, decoder_3to8_2_out_7, decoder_3to8_2_out_8, decoder_3to8_2_out_10, decoder_3to8_2_out_11, decoder_3to8_2_out_12);
  Decoder_3to8 decoder_3to8_1 (
    .in_1(in_1), .in_2(in_2), .in_3(in_3), .EN(not_1_out), .out_5(decoder_3to8_1_out_5),
    .out_6(decoder_3to8_1_out_6), .out_7(decoder_3to8_1_out_7), .out_8(decoder_3to8_1_out_8),
    .out_9(decoder_3to8_1_out_9), .out_10(decoder_3to8_1_out_10), .out_11(decoder_3to8_1_out_11),
    .out_12(decoder_3to8_1_out_12));
  Decoder_3to8 decoder_3to8_2 (
    .in_1(in_1), .in_2(in_2), .in_3(in_3), .EN(in_4), .out_5(decoder_3to8_2_out_5),
    .out_6(decoder_3to8_2_out_6), .out_7(decoder_3to8_2_out_7), .out_8(decoder_3to8_2_out_8),
    .out_9(decoder_3to8_2_out_9), .out_10(decoder_3to8_2_out_10), .out_11(decoder_3to8_2_out_11),
    .out_12(decoder_3to8_2_out_12));
  or a (a_out, decoder_3to8_1_out_11, decoder_3to8_1_out_5, decoder_3to8_1_out_7, decoder_3to8_1_out_8, decoder_3to8_1_out_10, decoder_3to8_1_out_12, decoder_3to8_2_out_5, decoder_3to8_2_out_6);
  or b (b_out, decoder_3to8_1_out_5, decoder_3to8_1_out_6, decoder_3to8_1_out_7, decoder_3to8_1_out_8, decoder_3to8_1_out_9, decoder_3to8_1_out_12, decoder_3to8_2_out_5, decoder_3to8_2_out_6);
  or c (c_out, decoder_3to8_1_out_5, decoder_3to8_1_out_6, decoder_3to8_1_out_8, decoder_3to8_1_out_9, decoder_3to8_1_out_10, decoder_3to8_1_out_11, decoder_3to8_1_out_12, decoder_3to8_2_out_5, decoder_3to8_2_out_6);
  or d (d_out, decoder_3to8_1_out_5, decoder_3to8_1_out_7, decoder_3to8_1_out_8, decoder_3to8_1_out_10, decoder_3to8_1_out_11, decoder_3to8_2_out_5);
  or e (e_out, decoder_3to8_1_out_5, decoder_3to8_1_out_7, decoder_3to8_1_out_11, decoder_3to8_2_out_5);
  or f (f_out, decoder_3to8_1_out_5, decoder_3to8_1_out_9, decoder_3to8_1_out_10, decoder_3to8_1_out_11, decoder_3to8_2_out_5, decoder_3to8_2_out_6);
  or g (g_out, decoder_3to8_1_out_7, decoder_3to8_1_out_8, decoder_3to8_1_out_9, decoder_3to8_1_out_10, decoder_3to8_1_out_11, decoder_3to8_2_out_5, decoder_3to8_2_out_6);
  _7_Segment_Display u_7_segment_display_1 (
    .g(g_out), .f(f_out), .a(a_out), .b(b_out), .e(e_out), .d(d_out), .c(c_out), .dp(or_1_out));
endmodule

module Decoder_2to4 (
  input  EN,
  input  in_2,
  input  in_3,
  output out_4,
  output out_5,
  output out_6,
  output out_7
);

  wire not_1_out, not_2_out;

  not not_1 (not_1_out, in_2);
  not not_2 (not_2_out, in_3);
  and and_1 (out_4, not_1_out, EN, not_2_out);
  and and_2 (out_5, in_2, EN, not_2_out);
  and and_3 (out_6, not_1_out, EN, in_3);
  and and_4 (out_7, in_2, EN, in_3);

  // Notes on the sheet:
  //   2- 4译码器
endmodule

module Decoder_3to8 (
  input  in_1,
  input  in_2,
  input  in_3,
  input  EN,
  output out_5,
  output out_6,
  output out_7,
  output out_8,
  output out_9,
  output out_10,
  output out_11,
  output out_12
);

  wire and_1_out, and_2_out, not_1_out;

  not not_1 (not_1_out, in_3);
  and and_1 (and_1_out, EN, not_1_out);
  and and_2 (and_2_out, in_3, EN);
  Decoder_2to4 decoder_2to4_1 (
    .EN(and_1_out), .in_2(in_1), .in_3(in_2), .out_4(out_5), .out_5(out_6), .out_6(out_7), .out_7(out_8));
  Decoder_2to4 decoder_2to4_2 (
    .EN(and_2_out), .in_2(in_1), .in_3(in_2), .out_4(out_9), .out_5(out_10), .out_6(out_11), .out_7(out_12));
endmodule

module SegmentDisplayDecoder_7 (
  input  in_1,
  input  in_2,
  input  in_3,
  input  in_4
);

  wire a_out, b_out, c_out, d_out, decoder_3to8_1_out_5, decoder_3to8_1_out_6, decoder_3to8_1_out_7,
       decoder_3to8_1_out_8, decoder_3to8_1_out_9, decoder_3to8_1_out_10, decoder_3to8_1_out_11,
       decoder_3to8_1_out_12, decoder_3to8_2_out_5, decoder_3to8_2_out_6, decoder_3to8_2_out_7,
       decoder_3to8_2_out_8, decoder_3to8_2_out_9, decoder_3to8_2_out_10, decoder_3to8_2_out_11,
       decoder_3to8_2_out_12, e_out, f_out, g_out, not_1_out, or_1_out;

  not not_1 (not_1_out, in_4);
  or or_1 (or_1_out, decoder_3to8_2_out_9, decoder_3to8_2_out_7, decoder_3to8_2_out_8, decoder_3to8_2_out_10, decoder_3to8_2_out_11, decoder_3to8_2_out_12);
  Decoder_3to8 decoder_3to8_1 (
    .in_1(in_1), .in_2(in_2), .in_3(in_3), .EN(not_1_out), .out_5(decoder_3to8_1_out_5),
    .out_6(decoder_3to8_1_out_6), .out_7(decoder_3to8_1_out_7), .out_8(decoder_3to8_1_out_8),
    .out_9(decoder_3to8_1_out_9), .out_10(decoder_3to8_1_out_10), .out_11(decoder_3to8_1_out_11),
    .out_12(decoder_3to8_1_out_12));
  Decoder_3to8 decoder_3to8_2 (
    .in_1(in_1), .in_2(in_2), .in_3(in_3), .EN(in_4), .out_5(decoder_3to8_2_out_5),
    .out_6(decoder_3to8_2_out_6), .out_7(decoder_3to8_2_out_7), .out_8(decoder_3to8_2_out_8),
    .out_9(decoder_3to8_2_out_9), .out_10(decoder_3to8_2_out_10), .out_11(decoder_3to8_2_out_11),
    .out_12(decoder_3to8_2_out_12));
  or a (a_out, decoder_3to8_1_out_11, decoder_3to8_1_out_5, decoder_3to8_1_out_7, decoder_3to8_1_out_8, decoder_3to8_1_out_10, decoder_3to8_1_out_12, decoder_3to8_2_out_5, decoder_3to8_2_out_6);
  or b (b_out, decoder_3to8_1_out_5, decoder_3to8_1_out_6, decoder_3to8_1_out_7, decoder_3to8_1_out_8, decoder_3to8_1_out_9, decoder_3to8_1_out_12, decoder_3to8_2_out_5, decoder_3to8_2_out_6);
  or c (c_out, decoder_3to8_1_out_5, decoder_3to8_1_out_6, decoder_3to8_1_out_8, decoder_3to8_1_out_9, decoder_3to8_1_out_10, decoder_3to8_1_out_11, decoder_3to8_1_out_12, decoder_3to8_2_out_5, decoder_3to8_2_out_6);
  or d (d_out, decoder_3to8_1_out_5, decoder_3to8_1_out_7, decoder_3to8_1_out_8, decoder_3to8_1_out_10, decoder_3to8_1_out_11, decoder_3to8_2_out_5);
  or e (e_out, decoder_3to8_1_out_5, decoder_3to8_1_out_7, decoder_3to8_1_out_11, decoder_3to8_2_out_5);
  or f (f_out, decoder_3to8_1_out_5, decoder_3to8_1_out_9, decoder_3to8_1_out_10, decoder_3to8_1_out_11, decoder_3to8_2_out_5, decoder_3to8_2_out_6);
  or g (g_out, decoder_3to8_1_out_7, decoder_3to8_1_out_8, decoder_3to8_1_out_9, decoder_3to8_1_out_10, decoder_3to8_1_out_11, decoder_3to8_2_out_5, decoder_3to8_2_out_6);
  _7_Segment_Display u_7_segment_display_1 (
    .g(g_out), .f(f_out), .a(a_out), .b(b_out), .e(e_out), .d(d_out), .c(c_out), .dp(or_1_out));
endmodule
