// Logisim project Comparator.circ as structural Verilog: 2 circuits, main circuit main
module main (
);

  wire comparator_4_1_out_9, dipswitch_1_p1, dipswitch_1_p2, dipswitch_1_p3, dipswitch_1_p4, dipswitch_2_p1,
       dipswitch_2_p2, dipswitch_2_p3, dipswitch_2_p4;

  // DipSwitch dipswitch_1: pin names not known; wires that end beside it: dipswitch_1_p1, dipswitch_1_p2, dipswitch_1_p3, dipswitch_1_p4
  // DipSwitch dipswitch_2: pin names not known; wires that end beside it: dipswitch_2_p1, dipswitch_2_p2, dipswitch_2_p3, dipswitch_2_p4
  LED led_1 (.in(comparator_4_1_out_9));
  Comparator_4 comparator_4_1 (
    .A0(dipswitch_1_p1), .B0(dipswitch_2_p1), .A1(dipswitch_1_p2), .B1(dipswitch_2_p2), .A2(dipswitch_1_p3),
    .B2(dipswitch_2_p3), .A3(dipswitch_1_p4), .B3(dipswitch_2_p4), .out_9(comparator_4_1_out_9));
endmodule

module Comparator_4 (
  input  A0,
  input  B0,
  input  A1,
  input  B1,
  input  A2,
  input  B2,
  input  A3,
  input  B3,
  output out_9
);

  wire not_1_out, not_2_out, not_3_out, not_4_out, xor_1_out, xor_2_out, xor_3_out, xor_4_out;

  xor xor_1 (xor_1_out, A0, B0);
  xor xor_2 (xor_2_out, A1, B1);
  xor xor_3 (xor_3_out, A2, B2);
  xor xor_4 (xor_4_out, A3, B3);
  not not_1 (not_1_out, xor_1_out);
  not not_2 (not_2_out, xor_2_out);
  not not_3 (not_3_out, xor_3_out);
  not not_4 (not_4_out, xor_4_out);
  and and_1 (out_9, not_1_out, not_2_out, not_3_out, not_4_out);
endmodule
