// Logisim project Decoder_3to5.circ as structural Verilog: 2 circuits, main circuit main
module main (
  input  in_1,
  input  in_2,
  input  in_3,
  output out_4,
  output out_5,
  output out_6,
  output out_7,
  output out_8,
  output out_9,
  output out_10,
  output out_11
);

  wire decoder_2to4_1_out_3, decoder_2to4_1_out_4, decoder_2to4_1_out_5, decoder_2to4_1_out_6,
       decoder_2to4_2_out_3, decoder_2to4_2_out_4, decoder_2to4_2_out_5, decoder_2to4_2_out_6, not_1_out;

  Decoder_2to4 decoder_2to4_1 (
    .in_1(in_1), .in_2(in_2), .out_3(decoder_2to4_1_out_3), .out_4(decoder_2to4_1_out_4),
    .out_5(decoder_2to4_1_out_5), .out_6(decoder_2to4_1_out_6));
  Decoder_2to4 decoder_2to4_2 (
    .in_1(in_1), .in_2(in_2), .out_3(decoder_2to4_2_out_3), .out_4(decoder_2to4_2_out_4),
    .out_5(decoder_2to4_2_out_5), .out_6(decoder_2to4_2_out_6));
  not not_1 (not_1_out, in_3);
  and and_1 (out_4, decoder_2to4_1_out_3, not_1_out);
  and and_2 (out_5, decoder_2to4_1_out_4, not_1_out);
  and and_3 (out_6, decoder_2to4_1_out_5, not_1_out);
  and and_4 (out_7, decoder_2to4_1_out_6, not_1_out);
  and and_5 (out_8, decoder_2to4_2_out_3, in_3);
  and and_6 (out_9, decoder_2to4_2_out_4, in_3);
  and and_7 (out_10, decoder_2to4_2_out_5, in_3);
  and and_8 (out_11, decoder_2to4_2_out_6, in_3);
endmodule

module Decoder_2to4 (
  input  in_1,
  input  in_2,
  output out_3,
  output out_4,
  output out_5,
  output out_6
);

  wire not_1_out, not_2_out;

  not not_1 (not_1_out, in_1);
  not not_2 (not_2_out, in_2);
  and and_1 (out_3, not_1_out, not_2_out);
  and and_2 (out_4, in_1, not_2_out);
  and and_3 (out_5, not_1_out, in_2);
  and and_4 (out_6, in_1, in_2);

  // Notes on the sheet:
  //   2- 4译码器
endmodule
