// Logisim project Decoder_5to32.circ as structural Verilog: 1 circuit, main circuit main
module main (
  input  in_1,
  input  in_2,
  input  in_3,
  input  in_4,
  input  in_5
);

  wire n74138_1_pin6, n74138_1_pin7, n74138_1_pin9, n74138_1_pin10, n74138_1_pin11, n74138_1_pin12,
       n74138_1_pin13, n74138_1_pin14, n74138_1_pin15, n74138_2_pin4, n74138_2_pin7, n74138_2_pin9,
       n74138_2_pin10, n74138_2_pin11, n74138_2_pin12, n74138_2_pin13, n74138_2_pin14, n74138_2_pin15,
       n74138_3_pin4, n74138_3_pin7, n74138_3_pin9, n74138_3_pin10, n74138_3_pin11, n74138_3_pin12,
       n74138_3_pin13, n74138_3_pin14, n74138_3_pin15, n74138_4_pin4, n74138_4_pin6, n74138_4_pin7,
       n74138_4_pin9, n74138_4_pin10, n74138_4_pin11, n74138_4_pin12, n74138_4_pin13, n74138_4_pin14,
       n74138_4_pin15;

  _74138 u_74138_1 (
    .pin1(in_1), .pin2(in_2), .pin3(in_3), .pin4(in_4), .pin5(in_5), .pin6(n74138_1_pin6),
    .pin7(n74138_1_pin7), .pin15(n74138_1_pin15), .pin14(n74138_1_pin14), .pin13(n74138_1_pin13),
    .pin12(n74138_1_pin12), .pin11(n74138_1_pin11), .pin10(n74138_1_pin10), .pin9(n74138_1_pin9));
  LED led_1 (.in(n74138_1_pin15));
  LED led_2 (.in(n74138_1_pin14));
  LED led_3 (.in(n74138_1_pin13));
  LED led_4 (.in(n74138_1_pin12));
  LED led_5 (.in(n74138_1_pin11));
  LED led_6 (.in(n74138_1_pin10));
  LED led_7 (.in(n74138_1_pin9));
  LED led_8 (.in(n74138_1_pin7));
  LED led_9 (.in(n74138_2_pin15));
  LED led_10 (.in(n74138_2_pin14));
  _74138 u_74138_2 (
    .pin1(in_1), .pin2(in_2), .pin3(in_3), .pin4(n74138_2_pin4), .pin5(in_5), .pin6(in_4),
    .pin7(n74138_2_pin7), .pin15(n74138_2_pin15), .pin14(n74138_2_pin14), .pin13(n74138_2_pin13),
    .pin12(n74138_2_pin12), .pin11(n74138_2_pin11), .pin10(n74138_2_pin10), .pin9(n74138_2_pin9));
  LED led_11 (.in(n74138_2_pin13));
  LED led_12 (.in(n74138_2_pin12));
  LED led_13 (.in(n74138_2_pin11));
  LED led_14 (.in(n74138_2_pin10));
  LED led_15 (.in(n74138_2_pin7));
  LED led_16 (.in(n74138_2_pin9));
  _74138 u_74138_3 (
    .pin1(in_1), .pin2(in_2), .pin3(in_3), .pin4(n74138_3_pin4), .pin5(in_4), .pin6(in_5),
    .pin7(n74138_3_pin7), .pin15(n74138_3_pin15), .pin14(n74138_3_pin14), .pin13(n74138_3_pin13),
    .pin12(n74138_3_pin12), .pin11(n74138_3_pin11), .pin10(n74138_3_pin10), .pin9(n74138_3_pin9));
  LED led_17 (.in(n74138_3_pin15));
  LED led_18 (.in(n74138_3_pin14));
  LED led_19 (.in(n74138_3_pin13));
  LED led_20 (.in(n74138_3_pin12));
  LED led_21 (.in(n74138_3_pin11));
  LED led_22 (.in(n74138_3_pin10));
  LED led_23 (.in(n74138_3_pin9));
  LED led_24 (.in(n74138_3_pin7));
  LED led_25 (.in(n74138_4_pin15));
  LED led_26 (.in(n74138_4_pin14));
  LED led_27 (.in(n74138_4_pin13));
  _74138 u_74138_4 (
    .pin1(in_1), .pin2(in_2), .pin3(in_3), .pin4(n74138_4_pin4), .pin5(n74138_4_pin4), .pin6(n74138_4_pin6),
    .pin7(n74138_4_pin7), .pin15(n74138_4_pin15), .pin14(n74138_4_pin14), .pin13(n74138_4_pin13),
    .pin12(n74138_4_pin12), .pin11(n74138_4_pin11), .pin10(n74138_4_pin10), .pin9(n74138_4_pin9));
  LED led_28 (.in(n74138_4_pin12));
  LED led_29 (.in(n74138_4_pin11));
  LED led_30 (.in(n74138_4_pin10));
  LED led_31 (.in(n74138_4_pin9));
  LED led_32 (.in(n74138_4_pin7));
  and and_1 (n74138_4_pin6, in_4, in_5);
  // also tied to GND on the sheet: {n74138_2_pin4, n74138_3_pin4, n74138_4_pin4}
  // also tied to VCC on the sheet: n74138_1_pin6
endmodule
