// Logisim project XOR.circ as structural Verilog: 1 circuit, main circuit main
module main (
  input  A,
  input  B,
  input  in_3,
  input  in_4,
  output out_5,
  output out_6
);

  wire and_1_out, and_2_out, and_3_out, and_4_out, not_1_out, not_2_out, not_3_out, not_4_out, or_2_out;

  and and_1 (and_1_out, A, not_1_out);
  not not_1 (not_1_out, B);
  not not_2 (not_2_out, A);
  and and_2 (and_2_out, not_2_out, B);
  and and_3 (and_3_out, in_3, not_3_out);
  not not_3 (not_3_out, in_4);
  not not_4 (not_4_out, in_3);
  and and_4 (and_4_out, not_4_out, in_4);
  or or_1 (out_5, and_1_out, and_2_out);
  or or_2 (or_2_out, and_3_out, and_4_out);
  not not_5 (out_6, or_2_out);

  // Notes on the sheet:
  //   异或门
  //   同或门
  //   18
  //   16
endmodule
